# Fritzing sketch Pico--shortcut-keyboard (saved by Fritzing 0.9.3b)
breadboards: 1

parts:
  Mod1 = Raspberry Pi Pico
  S1 = Momentary Switch [package=ksa_sealed_tac_switch]
  S2 = Momentary Switch [package=ksa_sealed_tac_switch]
  S3 = Momentary Switch [package=ksa_sealed_tac_switch]
  S4 = Momentary Switch [package=ksa_sealed_tac_switch]
  S5 = Momentary Switch [package=ksa_sealed_tac_switch]
  S6 = Momentary Switch [package=ksa_sealed_tac_switch]
  S7 = Momentary Switch [package=ksa_sealed_tac_switch]
  S8 = Momentary Switch [package=ksa_sealed_tac_switch]
  S9 = Momentary Switch [package=ksa_sealed_tac_switch]
  S10 = Momentary Switch [package=ksa_sealed_tac_switch]
  S11 = Momentary Switch [package=ksa_sealed_tac_switch]
  S12 = Momentary Switch [package=ksa_sealed_tac_switch]
  RE1 = Rotary Encoder [package=THT]
  JP1 = Header 4 [package=screwterminal-3.5mm-4_lock]

nets:
  N1: Mod1.pin_1, S1.1
  N2: Mod1.pin_2, S2.4
  N3: Mod1.pin_3, Mod1.pin_8, Mod1.pin_13, Mod1.pin_18, Mod1.pin_23, Mod1.pin_28, Mod1.pin_33, Mod1.pin_38, S5.2, S6.2, S7.2, S8.2, S9.2, S10.2, S11.2, S12.2, RE1.EncoderPinC
  N4: Mod1.pin_4, S3.4
  N5: Mod1.pin_5, S4.4
  N6: Mod1.pin_6, S5.4
  N7: Mod1.pin_7, S6.4
  N8: Mod1.pin_9, S7.4
  N9: Mod1.pin_10, S8.4
  N10: Mod1.pin_11, JP1.3
  N11: Mod1.pin_12, JP1.2
  N12: Mod1.pin_14, S9.4
  N13: Mod1.pin_15, S10.4
  N14: Mod1.pin_16, S11.4
  N15: Mod1.pin_17, S12.4
  N16: Mod1.pin_19, RE1.EncoderPinA
  N17: Mod1.pin_20, RE1.EncoderPinB
  N18: Mod1.pin_21, RE1.SwitchrPinD
  N19: Mod1.pin_36, S1.3, S2.2, S3.2, S4.2, S9.1, S10.1, S11.1, S12.1, RE1.SwitchPinE, JP1.4
  N20: Mod1.pin_40, JP1.1

custom parts:
  Raspberry Pi Pico: Raspberry Pi Pico. Based around the RP2040 microcontroller the Pico is a low cost microcontroller device bringing Raspberry Pi quality, cost, and easy of use to the microcontroller space. Jan 2021, Split part in to two versions: tht (this one) and SMD. This one will drill holes for a .1 in header in pcb to allow plugging in the module as well as providing pads to solder the module to the top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
  Rotary Encoder: Rotary Encoder from ALPSec11e with switch.
